// Logisim project jogo.circ as structural Verilog: 7 circuits, main circuit circuito_diferenca
module circuito_diferenca (
  input  [3:0] ESCOLHA_CPU_B,
  input  [3:0] ESCOLHA_USUARIO_A,
  output [3:0] DISTANCIA
);

  wire and_1_out, and_2_out, and_3_out, and_4_out, and_5_out, and_6_out, and_7_out, and_8_out, and_9_out,
       and_10_out, and_11_out, and_12_out, and_13_out, and_14_out, and_15_out, and_16_out, and_17_out,
       and_18_out, and_19_out, and_20_out, not_1_out, not_2_out, not_3_out, not_4_out, not_5_out, not_6_out,
       not_7_out, not_8_out, not_9_out, not_10_out, not_11_out, not_12_out, not_13_out, not_14_out, or_1_out,
       or_2_out, or_3_out, or_4_out, or_6_out, xor_1_out, xor_2_out, xor_3_out, xor_4_out, xor_5_out,
       xor_6_out;
  wire [3:0] and_21_out, and_22_out, not_15_out, xor_7_out, xor_8_out;
  wire [3:3] or_5_out;

  xor xor_1 (xor_1_out, ESCOLHA_CPU_B[1], ESCOLHA_USUARIO_A[1]);
  not not_1 (not_1_out, ESCOLHA_USUARIO_A[1]);
  not not_2 (not_2_out, ESCOLHA_USUARIO_A[1]);
  xor xor_2 (xor_2_out, ESCOLHA_USUARIO_A[1], ESCOLHA_CPU_B[1]);
  not not_3 (not_3_out, ESCOLHA_CPU_B[1]);
  not not_4 (not_4_out, ESCOLHA_CPU_B[1]);
  xor xor_3 (xor_3_out, ESCOLHA_CPU_B[2], ESCOLHA_USUARIO_A[2]);
  not not_5 (not_5_out, ESCOLHA_USUARIO_A[2]);
  not not_6 (not_6_out, ESCOLHA_USUARIO_A[2]);
  not not_7 (not_7_out, ESCOLHA_CPU_B[2]);
  not not_8 (not_8_out, ESCOLHA_CPU_B[2]);
  not not_9 (not_9_out, ESCOLHA_USUARIO_A[0]);
  not not_10 (not_10_out, ESCOLHA_CPU_B[0]);
  and and_1 (and_1_out, and_19_out, ESCOLHA_CPU_B[1]);
  and and_2 (and_2_out, and_19_out, not_1_out);
  and and_3 (and_3_out, not_2_out, ESCOLHA_CPU_B[1]);
  and and_4 (and_4_out, and_20_out, ESCOLHA_USUARIO_A[1]);
  and and_5 (and_5_out, and_20_out, not_3_out);
  and and_6 (and_6_out, not_4_out, ESCOLHA_USUARIO_A[1]);
  and and_7 (and_7_out, or_1_out, ESCOLHA_CPU_B[2]);
  and and_8 (and_8_out, or_1_out, not_5_out);
  and and_9 (and_9_out, not_6_out, ESCOLHA_CPU_B[2]);
  xor xor_4 (xor_4_out, ESCOLHA_CPU_B[2], ESCOLHA_USUARIO_A[2]);
  and and_10 (and_10_out, or_2_out, ESCOLHA_USUARIO_A[2]);
  and and_11 (and_11_out, or_2_out, not_7_out);
  and and_12 (and_12_out, not_8_out, ESCOLHA_USUARIO_A[2]);
  xor xor_5 (xor_5_out, ESCOLHA_CPU_B[3], ESCOLHA_USUARIO_A[3]);
  and and_13 (and_13_out, or_3_out, ESCOLHA_CPU_B[3]);
  and and_14 (and_14_out, or_3_out, not_11_out);
  not not_11 (not_11_out, ESCOLHA_USUARIO_A[3]);
  not not_12 (not_12_out, ESCOLHA_USUARIO_A[3]);
  and and_15 (and_15_out, not_12_out, ESCOLHA_CPU_B[3]);
  xor xor_6 (xor_6_out, ESCOLHA_USUARIO_A[3], ESCOLHA_CPU_B[3]);
  and and_16 (and_16_out, or_4_out, ESCOLHA_USUARIO_A[3]);
  and and_17 (and_17_out, or_4_out, not_13_out);
  not not_13 (not_13_out, ESCOLHA_CPU_B[3]);
  not not_14 (not_14_out, ESCOLHA_CPU_B[3]);
  and and_18 (and_18_out, not_14_out, ESCOLHA_USUARIO_A[3]);
  xor xor_7 (xor_7_out[0], ESCOLHA_CPU_B[0], ESCOLHA_USUARIO_A[0]);
  and and_19 (and_19_out, not_9_out, ESCOLHA_CPU_B[0]);
  xor xor_8 (xor_8_out[0], ESCOLHA_CPU_B[0], ESCOLHA_USUARIO_A[0]);
  and and_20 (and_20_out, not_10_out, ESCOLHA_USUARIO_A[0]);
  xor xor_9 (xor_7_out[1], xor_1_out, and_19_out);
  or or_1 (or_1_out, and_1_out, and_2_out, and_3_out);
  xor xor_10 (xor_8_out[1], xor_2_out, and_20_out);
  or or_2 (or_2_out, and_4_out, and_5_out, and_6_out);
  xor xor_11 (xor_7_out[2], xor_3_out, or_1_out);
  or or_3 (or_3_out, and_7_out, and_8_out, and_9_out);
  xor xor_12 (xor_8_out[2], xor_4_out, or_2_out);
  or or_4 (or_4_out, and_10_out, and_11_out, and_12_out);
  xor xor_13 (xor_7_out[3], xor_5_out, or_3_out);
  or or_5 (or_5_out[3], and_13_out, and_14_out, and_15_out);
  xor xor_14 (xor_8_out[3], xor_6_out, or_4_out);
  or or_6 (or_6_out, and_16_out, and_17_out, and_18_out);
  assign not_15_out = ~{4{or_5_out[3]}};  // NOT_Gate not_15, 4 bits wide
  assign and_21_out = xor_7_out & not_15_out;  // AND_Gate and_21, 4 bits wide
  assign and_22_out = xor_8_out & {4{or_5_out[3]}};  // AND_Gate and_22, 4 bits wide
  assign DISTANCIA = and_21_out | and_22_out;  // OR_Gate or_7, 4 bits wide

  // Notes on the sheet:
  //   BIT 0 (B)
  //   BIT 0 (A)
  //   BIT 1 (B)
  //   BIT 1 (A)
  //   BIT 2 (B)
  //   BIT 2 (A)
  //   BIT 3 (B)
  //   BIT 3 (A)
  //   B.I. BIT 1 (B - A)
  //   B.I. BIT 2 (A - B)
  //   B.I. BIT 1 (A - B)
  //   B.I. BIT 2 (B - A)
  //   BIT 0 PARA (A - B)
  //   BIT 0 PARA (B - A)
  //   BIT 1 PARA (A - B)
  //   BIT 1 PARA (B-A)
  //   BIT 2 PARA (A - B)
  //   BIT 2 PARA (B-A)
  //   BIT 3 PARA (A - B)
  //   BIT 3 PARA (B-A)
  //   DIFF 0 (A - B)
  //   BOUT
  //   DIFF 0 (B - A)
  //   BOUT
  //   DIFF 1 (A - B)
  //   BOUT
  //   DIFF 1 (B - A)
  //   BOUT
  //   DIFF 2 (A - B)
  //   BOUT
  //   DIFF 2 (B - A)
  //   BOUT
  //   DIFF 3 (A - B)
  //   BOUT
  //   DIFF 3 (B - A)
  //   BOUT FINAL SEM USO (EM ANÁLISE)´
  //   Ditribuidor (A-B)
  //   Distribuidos (B - A)
  //   Transformando o Bout 
  //   em um número 4 bits
  //   MULTIPLEXADOR (2X1)
endmodule

module circuito_comparador (
  input  [3:0] ESCOLHA_CPU_B,
  input  [3:0] ESCOLHA_USUARIO_A,
  output IGUALDADE
);

  wire xnor_1_out, xnor_2_out, xnor_3_out, xnor_4_out;

  xnor xnor_1 (xnor_1_out, ESCOLHA_CPU_B[0], ESCOLHA_USUARIO_A[0]);
  xnor xnor_2 (xnor_2_out, ESCOLHA_CPU_B[1], ESCOLHA_USUARIO_A[1]);
  xnor xnor_3 (xnor_3_out, ESCOLHA_CPU_B[2], ESCOLHA_USUARIO_A[2]);
  xnor xnor_4 (xnor_4_out, ESCOLHA_CPU_B[3], ESCOLHA_USUARIO_A[3]);
  and and_1 (IGUALDADE, xnor_1_out, xnor_2_out, xnor_3_out, xnor_4_out);

  // Notes on the sheet:
  //   COMPARA BIT 0
  //   COMPARA BIT 1
  //   COMPARA BIT 2
  //   COMPARA BIT 3
  //   COMPARA TODO
  //   O NÚMERO
endmodule

module circuito_cores (
  input  [3:0] DIFERENCA,
  output [7:0] S1,
  output [7:0] S2
);

  not not_1 (S1[4], DIFERENCA[0]);
  not not_2 (S1[5], DIFERENCA[1]);
  not not_3 (S1[6], DIFERENCA[2]);
  not not_4 (S1[7], DIFERENCA[3]);

  assign S1[3:0] = 4'b0000;
  assign S2 = {DIFERENCA, 4'b0000};

  // Notes on the sheet:
  //   BITS MENOS
  //   SIGNIFICATIVOS
  //   BITS PRA S1
  //   VERMELHO
  //   AZUL
endmodule

module subcircuito_extensor (
  input  ENTRADA,
  output [7:0] SAIDA
);


  assign SAIDA = {8{ENTRADA}};
endmodule

module circuito_decoder (
  input  A,
  input  B,
  input  C,
  input  D,
  output up1,
  output up2,
  output up3,
  output up4,
  output down1,
  output down2,
  output down3,
  output down4
);

  wire and_1_out, and_2_out, and_3_out, and_4_out, and_5_out, and_6_out, and_7_out, and_8_out, and_9_out,
       and_10_out, and_11_out, and_12_out, and_13_out, and_14_out, and_15_out, and_16_out, and_17_out,
       and_18_out, and_19_out, and_20_out, and_21_out, and_22_out, and_23_out, and_24_out, and_25_out,
       and_26_out, and_27_out, and_28_out, and_29_out, and_30_out, and_31_out, and_32_out, and_33_out,
       and_34_out, and_35_out, not_1_out, not_2_out, not_3_out, not_4_out;

  not not_1 (not_1_out, A);
  not not_2 (not_2_out, B);
  not not_3 (not_3_out, C);
  not not_4 (not_4_out, D);
  and and_1 (and_1_out, not_2_out, not_4_out);
  and and_2 (and_2_out, not_1_out, C);
  and and_3 (and_3_out, not_1_out, B, D);
  and and_4 (and_4_out, A, not_2_out, not_3_out);
  and and_5 (and_5_out, A, not_4_out);
  and and_6 (and_6_out, B, C);
  and and_7 (and_7_out, not_1_out, not_3_out, not_4_out);
  and and_8 (and_8_out, not_1_out, C, D);
  and and_9 (and_9_out, not_2_out, not_4_out);
  and and_10 (and_10_out, A, not_3_out, D);
  and and_11 (and_11_out, not_1_out, not_2_out);
  and and_12 (and_12_out, not_1_out, B);
  and and_13 (and_13_out, A, not_2_out);
  and and_14 (and_14_out, not_3_out, D);
  and and_15 (and_15_out, not_2_out, not_3_out);
  and and_16 (and_16_out, not_2_out, D);
  and and_17 (and_17_out, B, not_3_out, D);
  and and_18 (and_18_out, not_1_out, not_2_out, not_4_out);
  and and_19 (and_19_out, not_2_out, C, D);
  and and_20 (and_20_out, A, not_3_out);
  and and_21 (and_21_out, B, C, not_4_out);
  and and_22 (and_22_out, not_2_out, not_4_out);
  and and_23 (and_23_out, C, not_4_out);
  and and_24 (and_24_out, A, C);
  and and_25 (and_25_out, A, B);
  and and_26 (and_26_out, not_3_out, not_4_out);
  and and_27 (and_27_out, not_1_out, B, not_3_out);
  and and_28 (and_28_out, B, not_4_out);
  and and_29 (and_29_out, A, not_2_out);
  and and_30 (and_30_out, A, C);
  and and_31 (and_31_out, not_2_out, C);
  and and_32 (and_32_out, A, not_2_out);
  and and_33 (and_33_out, not_1_out, B, not_3_out);
  and and_34 (and_34_out, C, not_4_out);
  and and_35 (and_35_out, A, D);
  or or_1 (up3, and_1_out, and_2_out, and_3_out, and_4_out, and_5_out, and_6_out);
  or or_2 (up4, and_7_out, and_8_out, and_9_out, and_10_out, and_11_out);
  or or_3 (down3, and_12_out, and_13_out, and_14_out, and_15_out, and_16_out);
  or or_4 (down2, and_17_out, and_18_out, and_19_out, and_20_out, and_21_out);
  or or_5 (down1, and_22_out, and_23_out, and_24_out, and_25_out);
  or or_6 (up2, and_26_out, and_27_out, and_28_out, and_29_out, and_30_out);
  or or_7 (up1, and_31_out, and_32_out, and_33_out, and_34_out, and_35_out);

  assign down4 = 1'b0;

  // Notes on the sheet:
  //   UP 1
  //   UP 2
  //   UP 3
  //   UP 4
  //   DOWN 1
  //   DOWN 2
  //   DOWN 3
  //   DOWN 4
endmodule

module circuito_guess (
  input  CONFIRMAR,
  input  novo,
  input  [3:0] CHUTE,
  output verde,
  output [7:0] VERMELHO,
  output [7:0] AZUL,
  output ACERTOU
);

  wire COMPARADOR_igualdade;
  wire [3:0] DIFERENCA_distancia, random_1_out;
  wire [7:0] circuito_cores_1_s1, circuito_cores_1_s2, sinal_extendido_saida;

  Random #(.width(4)) random_1 (.clk(novo), .out(random_1_out));  // open: clr, next
  circuito_diferenca DIFERENCA (
    .ESCOLHA_USUARIO_A(random_1_out), .ESCOLHA_CPU_B(CHUTE), .DISTANCIA(DIFERENCA_distancia));
  subcircuito_extensor sinal_extendido (.ENTRADA(CONFIRMAR), .SAIDA(sinal_extendido_saida));
  circuito_comparador COMPARADOR (
    .ESCOLHA_CPU_B(CHUTE), .ESCOLHA_USUARIO_A(random_1_out), .IGUALDADE(COMPARADOR_igualdade));
  assign VERMELHO = sinal_extendido_saida & circuito_cores_1_s1;  // AND_Gate and_1, 8 bits wide
  circuito_cores circuito_cores_1 (.DIFERENCA(DIFERENCA_distancia), .S1(circuito_cores_1_s1), .S2(circuito_cores_1_s2));
  assign AZUL = circuito_cores_1_s2 & sinal_extendido_saida;  // AND_Gate and_2, 8 bits wide
  and and_3 (ACERTOU, CONFIRMAR, COMPARADOR_igualdade);

  assign verde = 1'b0;

  // Notes on the sheet:
  //   1 para 8 BITS
endmodule

module main (
  input  CONFIRMAR,
  input  [3:0] CHUTE,
  input  novo
);

  wire circuito_decoder_1_down1, circuito_decoder_1_down2, circuito_decoder_1_down3,
       circuito_decoder_1_down4, circuito_decoder_1_up1, circuito_decoder_1_up2, circuito_decoder_1_up3,
       circuito_decoder_1_up4, circuito_guess_1_acertou, circuito_guess_1_verde;
  wire [7:0] circuito_guess_1_azul, circuito_guess_1_vermelho;

  circuito_guess circuito_guess_1 (
    .CONFIRMAR(CONFIRMAR), .novo(novo), .CHUTE(CHUTE), .verde(circuito_guess_1_verde),
    .VERMELHO(circuito_guess_1_vermelho), .AZUL(circuito_guess_1_azul), .ACERTOU(circuito_guess_1_acertou));
  circuito_decoder circuito_decoder_1 (
    .A(CHUTE[3]), .B(CHUTE[2]), .C(CHUTE[1]), .D(CHUTE[0]), .up1(circuito_decoder_1_up1),
    .up2(circuito_decoder_1_up2), .up3(circuito_decoder_1_up3), .up4(circuito_decoder_1_up4),
    .down1(circuito_decoder_1_down1), .down2(circuito_decoder_1_down2), .down3(circuito_decoder_1_down3),
    .down4(circuito_decoder_1_down4));
  LED acertou (.in(circuito_guess_1_acertou));
  _7_Segment_Display display (
    .g(circuito_decoder_1_up1), .f(circuito_decoder_1_up2), .a(circuito_decoder_1_up3),
    .b(circuito_decoder_1_up4), .e(circuito_decoder_1_down1), .d(circuito_decoder_1_down2),
    .c(circuito_decoder_1_down3), .dp(circuito_decoder_1_down4));
  // RGBLED rgbled_1: pin names not known; wires that end beside it: circuito_guess_1_vermelho[7], circuito_guess_1_azul[7]
  // RGBLED rgbled_2: pin names not known; wires that end beside it: circuito_guess_1_vermelho[6], circuito_guess_1_azul[6]
  // RGBLED rgbled_3: pin names not known; wires that end beside it: circuito_guess_1_vermelho[5], circuito_guess_1_azul[5]
  // RGBLED rgbled_4: pin names not known; wires that end beside it: circuito_guess_1_verde, circuito_guess_1_vermelho[4], circuito_guess_1_azul[4]
endmodule
